# Fritzing sketch Lesson 1  Blinking LED (saved by Fritzing 0.8.7b)
breadboards: 1

parts:
  LED1 = LED - 5mm [color="Red (633nm)" package="5 mm [THT]"]
  R2 = Resistor [tolerance=±5% resistance=220 package=THT]
  T-Extension1 = T_Extension

nets:
  N1: LED1.cathode, T-Extension1.B17
  N2: LED1.anode, R2.Pin_0
  N3: R2.Pin_1, T-Extension1.3V3#0

notes:
  +

custom parts:
  T_Extension: T-Extension Board for RPi B+ and Rpi2 from SunFounder
