# Fritzing sketch Lesson 10 Slide Switch (saved by Fritzing 0.8.7b)
breadboards: 1

parts:
  R1 = Resistor [tolerance=±5% resistance=10k package=THT]
  C1 = Ceramic Capacitor [capacitance=100nF package="100 mil [THT, multilayer]"]
  S1 = Toggle Switch [package=THT]
  LED1 = LED - 5mm [color="Red (633nm)" package="5 mm [THT]"]
  R2 = Resistor [tolerance=±5% resistance=220 package=THT]
  T-Extension1 = T_Extension
  LED2 = LED - 5mm [color="Green (565nm)" package="5 mm [THT]"]
  R3 = Resistor [tolerance=±5% resistance=220 package=THT]

nets:
  N1: R1.Pin_0, C1.0, S1.COM, T-Extension1.B17
  N2: R1.Pin_1, C1.1, S1.L2, T-Extension1.GND#36
  N3: S1.L1, R2.Pin_1, T-Extension1.3V3#0, R3.Pin_0
  N4: LED1.cathode, T-Extension1.B18
  N5: LED1.anode, R2.Pin_0
  N6: T-Extension1.B27, LED2.cathode
  N7: LED2.anode, R3.Pin_1

notes:
  104

custom parts:
  T_Extension: T-Extension Board for RPi B+ and Rpi2 from SunFounder
