# Fritzing sketch Lesson 12  Rotary Encoder (saved by Fritzing 0.9.3b)
breadboards: 1

parts:
  module2 = Rotary Encoder
  R1 = Resistor [tolerance=±5% resistance=10k package=THT]
  T-Extension2 = T_Extension

nets:
  N1: module2.CLK, T-Extension2.B17
  N2: module2.DT, T-Extension2.B18
  VCC: module2.VCC, T-Extension2.5V
  N3: module2.GND, T-Extension2.GND#37
  N4: module2.SW, R1.Pin_1, T-Extension2.B27
  N5: R1.Pin_0, T-Extension2.3V3#0

notes:
  Rotary Encoder

custom parts:
  Rotary Encoder: Rotary Encoder module of SunFounder Sensor Kit
  T_Extension: T-Extension Board for RPi B+ and Rpi2 from SunFounder
