# Fritzing sketch Lesson 12  Rotary Encoder (saved by Fritzing 0.9.3b)
breadboards: 1

parts:
  module2 = Rotary Encoder
  T-Extension1 = T_Extension
  R1 = Resistor [tolerance=±5% resistance=10k package=THT]

nets:
  N1: module2.CLK, T-Extension1.B17
  N2: module2.DT, T-Extension1.B18
  VCC: module2.VCC, T-Extension1.5V
  N3: module2.GND, T-Extension1.GND#37
  N4: module2.SW, T-Extension1.B27, R1.Pin_1
  N5: T-Extension1.3V3#0, R1.Pin_0

notes:
  Rotary Encoder

custom parts:
  Rotary Encoder: Rotary Encoder module of SunFounder Sensor Kit
  T_Extension: T-Extension Board for RPi B+ and Rpi2 from SunFounder
