# Fritzing sketch Lesson 13  Driving LEDs by 74HC595 (saved by Fritzing 0.8.7b)
breadboards: 1

parts:
  R1 = Resistor [tolerance=±5% resistance=220 package=THT]
  R2 = Resistor [tolerance=±5% resistance=220 package=THT]
  R3 = Resistor [tolerance=±5% resistance=220 package=THT]
  R4 = Resistor [tolerance=±5% resistance=220 package=THT]
  R5 = Resistor [tolerance=±5% resistance=220 package=THT]
  R6 = Resistor [tolerance=±5% resistance=220 package=THT]
  R7 = Resistor [tolerance=±5% resistance=220 package=THT]
  R8 = Resistor [tolerance=±5% resistance=220 package=THT]
  LED1 = LED - 5mm [color="Red (633nm)" package="5 mm [THT]"]
  LED2 = LED - 5mm [color="Green (570nm)" package="5 mm [THT]"]
  LED3 = LED - 5mm [color="Yellow (595nm)" package="5 mm [THT]"]
  LED4 = LED - 5mm [color="Green (570nm)" package="5 mm [THT]"]
  LED5 = LED - 5mm [color="Red (633nm)" package="5 mm [THT]"]
  LED6 = LED - 5mm [color="Red (633nm)" package="5 mm [THT]"]
  LED7 = LED - 5mm [color="Yellow (595nm)" package="5 mm [THT]"]
  LED8 = LED - 5mm [color="Red (633nm)" package="5 mm [THT]"]
  U1 = 74HC595 SMD [package="SO16 [SMD]"]
  T-Extension1 = T_Extension

nets:
  N1: R1.Pin_0, LED1.anode
  N2: R1.Pin_1, U1.Q0
  N3: R2.Pin_0, LED2.anode
  N4: R2.Pin_1, U1.Q2
  N5: R3.Pin_0, LED4.anode
  N6: R3.Pin_1, U1.Q3
  N7: R4.Pin_0, LED6.anode
  N8: R4.Pin_1, U1.Q1
  N9: R5.Pin_0, LED7.anode
  N10: R5.Pin_1, U1.Q4
  N11: R6.Pin_0, LED3.anode
  N12: R6.Pin_1, U1.Q5
  N13: R7.Pin_0, LED5.anode
  N14: R7.Pin_1, U1.Q6
  N15: R8.Pin_0, LED8.anode
  N16: R8.Pin_1, U1.Q7
  N17: LED1.cathode, LED2.cathode, LED3.cathode, LED4.cathode, LED5.cathode, LED6.cathode, LED7.cathode, LED8.cathode, U1.GND, T-Extension1.GND#36
  VCC: U1.MR, U1.VCC, T-Extension1.5V
  N18: U1.SH_CP, T-Extension1.B27
  N19: U1.ST_CP, T-Extension1.B18
  N20: U1.OE, T-Extension1.GND#37
  N21: U1.DS, T-Extension1.B17

notes:
  +

custom parts:
  T_Extension: T-Extension Board for RPi B+ and Rpi2 from SunFounder
