# Fritzing sketch Lesson 14  Driving 7-Segment Display by 74HC595(button) (saved by Fritzing 0.9.3b)
breadboards: 1

parts:
  DI1 = 7-Segment LED Display [package=THT]
  U1 = 74HC595 SMD [package="SO16 [SMD]"]
  R1 = Resistor [tolerance=±5% resistance=220 package=THT]
  T-Extension1 = T_Extension
  S1 = Pushbutton [package="[THT]"]
  R2 = Resistor [tolerance=±5% resistance=10k package=THT]

nets:
  N1: DI1.cathodeE, U1.Q4
  N2: DI1.cathodeD, U1.Q3
  N3: DI1.commAnode#2, R1.Pin_1
  N4: DI1.cathodeC, U1.Q2
  N5: DI1.cathodeDP, U1.Q7
  N6: DI1.cathodeB, U1.Q1
  N7: DI1.cathodeA, U1.Q0
  N8: DI1.cathodeF, U1.Q5
  N9: DI1.cathodeG, U1.Q6
  N10: U1.GND, R1.Pin_0, T-Extension1.GND#36, S1.Pin_1, S1.Pin_2
  VCC: U1.MR, U1.VCC, T-Extension1.5V
  N11: U1.SH_CP, T-Extension1.B27
  N12: U1.ST_CP, T-Extension1.B18
  N13: U1.OE, T-Extension1.GND#37
  N14: U1.DS, T-Extension1.B17
  N15: T-Extension1.3V3#0, R2.Pin_1
  N16: T-Extension1.B22, S1.Pin_3, S1.Pin_4, R2.Pin_0

custom parts:
  T_Extension: T-Extension Board for RPi B+ and Rpi2 from SunFounder
