# Fritzing sketch Lesson 15  Driving Dot-Matrix by 74HC5952  (saved by Fritzing 0.9.3b)
breadboards: 1

parts:
  U1 = 74HC595 [package="DIP16 [THT]"]
  U2 = 74HC595 [package="DIP16 [THT]"]
  T-Extension1 = T_Extension

nets:
  GND: U1.GND, U2.GND, T-Extension1.GND#36
  VCC: U1.MR, U1.DS, U1.VCC, U2.MR, U2.VCC, T-Extension1.5V
  N1: U1.SH_CP, U2.SH_CP, T-Extension1.B27
  N2: U1.ST_CP, U2.ST_CP, T-Extension1.B18
  N3: U1.OE, U2.OE, T-Extension1.3V3#0
  N4: U2.DS, T-Extension1.B17

custom parts:
  T_Extension: T-Extension Board for RPi B+ and Rpi2 from SunFounder
