# Fritzing sketch Lesson 15  Driving Dot-Matrix by 74HC5953  (saved by Fritzing 0.9.3b)
breadboards: 1

parts:
  U1 = 74HC595 [package="DIP16 [THT]"]
  U2 = 74HC595 [package="DIP16 [THT]"]
  module1 = 788BS Dot matix
  T-Extension1 = T_Extension

nets:
  N1: U1.Q1, module1.P3
  N2: U1.Q2, module1.P4
  N3: U1.Q3, module1.P10
  N4: U1.Q4, module1.P6
  N5: U1.Q5, module1.P11
  N6: U1.Q6, module1.P15
  N7: U1.Q7, module1.P16
  GND: U1.GND, U2.GND, T-Extension1.GND#36
  VCC: U1.MR, U1.VCC, U2.MR, U2.VCC, T-Extension1.5V
  N8: U1.SH_CP, U2.SH_CP, T-Extension1.B27
  N9: U1.ST_CP, U2.ST_CP, T-Extension1.B18
  N10: U1.OE, U2.OE, T-Extension1.GND#37
  N11: U1.DS, U2.Q7'
  N12: U1.Q0, module1.P13
  N13: U2.DS, T-Extension1.B17

custom parts:
  788BS Dot matix: 788BS 8x8 dot matix from SunFounder
  T_Extension: T-Extension Board for RPi B+ and Rpi2 from SunFounder
