# Fritzing sketch Lesson 16  LCD1602 (saved by Fritzing 0.8.7b)
breadboards: 1

parts:
  LCD1 = LCD screen
  U1 = POT [package=alps_pot]
  T-Extension1 = T_Extension

nets:
  N1: LCD1.VSS, LCD1.R/W, LCD1.LED-, U1.A, T-Extension1.GND#36
  VDD: LCD1.VDD, U1.E, T-Extension1.5V
  N2: LCD1.V0, U1.S
  N3: LCD1.RS, T-Extension1.B27
  N4: LCD1.E, T-Extension1.B22
  N5: LCD1.DB4, T-Extension1.B25
  N6: LCD1.DB5, T-Extension1.B24
  N7: LCD1.DB6, T-Extension1.B23
  N8: LCD1.DB7, T-Extension1.B18
  N9: LCD1.LED+, T-Extension1.3V3#0

custom parts:
  T_Extension: T-Extension Board for RPi B+ and Rpi2 from SunFounder
