# Fritzing sketch Lesson 17  ADXL345 (saved by Fritzing 0.9.3b)
breadboards: 1

parts:
  3-axis_accelerometer3 = ADXL345 [package=THT]
  T-Extension1 = T_Extension

nets:
  N1: 3-axis_accelerometer3.GND, T-Extension1.GND#36
  N2: 3-axis_accelerometer3.VCC, T-Extension1.3V3#0
  N3: 3-axis_accelerometer3.SDA, T-Extension1.SDA
  N4: 3-axis_accelerometer3.SCL, T-Extension1.SCL

custom parts:
  ADXL345: An ADXL345 is a small, thin, low power, 3-axis accelerometer with high resolution (13-bit) measurement at up to ±16 g. Digital output data is formatted as 16-bit two’s complement and is accessible through either an SPI (3- or 4-wire) or I2C digital interface.
  T_Extension: T-Extension Board for RPi B+ and Rpi2 from SunFounder
