# Fritzing sketch Lesson 17  ADXL345 (saved by Fritzing 0.9.3b)
breadboards: 1

parts:
  T-Extension1 = T_Extension
  3-axis_accelerometer3 = ADXL345 [package=THT]

nets:
  N1: T-Extension1.3V3#0, 3-axis_accelerometer3.VCC
  N2: T-Extension1.SDA, 3-axis_accelerometer3.SDA
  N3: T-Extension1.SCL, 3-axis_accelerometer3.SCL
  N4: T-Extension1.GND#36, 3-axis_accelerometer3.GND

custom parts:
  T_Extension: T-Extension Board for RPi B+ and Rpi2 from SunFounder
  ADXL345: An ADXL345 is a small, thin, low power, 3-axis accelerometer with high resolution (13-bit) measurement at up to ±16 g. Digital output data is formatted as 16-bit two’s complement and is accessible through either an SPI (3- or 4-wire) or I2C digital interface.
