# Fritzing sketch Lesson 2  Controlling an LED by a Button (saved by Fritzing 0.9.3b)
breadboards: 1

parts:
  LED1 = LED - 5mm [color="Red (633nm)" package="5 mm [THT]"]
  R2 = Resistor [tolerance=±5% resistance=220 package=THT]
  S1 = Pushbutton [package="[THT]"]
  R3 = Resistor [tolerance=±5% resistance=10k package=THT]
  T-Extension1 = T_Extension

nets:
  N1: LED1.cathode, T-Extension1.B17
  N2: LED1.anode, R2.Pin_0
  N3: R2.Pin_1, R3.Pin_0, T-Extension1.3V3#0
  N4: S1.Pin_1, S1.Pin_2, T-Extension1.GND#36
  N5: S1.Pin_3, S1.Pin_4, R3.Pin_1, T-Extension1.B18

notes:
  -
  +

custom parts:
  T_Extension: T-Extension Board for RPi B+ and Rpi2 from SunFounder
