# Fritzing sketch Lesson 3  Flowing LED Lights (saved by Fritzing 0.8.7b)
breadboards: 1

parts:
  LED1 = LED - 5mm [color="Red (633nm)" package="5 mm [THT]"]
  LED2 = LED - 5mm [color="Red (633nm)" package="5 mm [THT]"]
  LED3 = LED - 5mm [color="Yellow (595nm)" package="5 mm [THT]"]
  LED4 = LED - 5mm [color="Yellow (595nm)" package="5 mm [THT]"]
  LED5 = LED - 5mm [color="Red (633nm)" package="5 mm [THT]"]
  LED6 = LED - 5mm [color="Red (633nm)" package="5 mm [THT]"]
  LED7 = LED - 5mm [color="Green (560nm)" package="5 mm [THT]"]
  LED8 = LED - 5mm [color="Green (565nm)" package="5 mm [THT]"]
  R9 = Resistor [tolerance=±5% resistance=220 package=THT]
  R11 = Resistor [tolerance=±5% resistance=220 package=THT]
  R12 = Resistor [tolerance=±5% resistance=220 package=THT]
  R13 = Resistor [tolerance=±5% resistance=220 package=THT]
  R14 = Resistor [tolerance=±5% resistance=220 package=THT]
  R15 = Resistor [tolerance=±5% resistance=220 package=THT]
  R16 = Resistor [tolerance=±5% resistance=220 package=THT]
  R17 = Resistor [tolerance=±5% resistance=220 package=THT]
  T-Extension1 = T_Extension

nets:
  N1: LED1.cathode, T-Extension1.B17
  N2: LED1.anode, R11.Pin_0
  N3: LED2.cathode, T-Extension1.B18
  N4: LED2.anode, R12.Pin_0
  N5: LED3.cathode, T-Extension1.B27
  N6: LED3.anode, R13.Pin_0
  N7: LED4.cathode, T-Extension1.B22
  N8: LED4.anode, R14.Pin_0
  N9: LED5.cathode, T-Extension1.B25
  N10: LED5.anode, R17.Pin_0
  N11: LED6.cathode, T-Extension1.B4
  N12: LED6.anode, R9.Pin_0
  N13: LED7.cathode, T-Extension1.B23
  N14: LED7.anode, R15.Pin_0
  N15: LED8.cathode, T-Extension1.B24
  N16: LED8.anode, R16.Pin_0
  N17: R9.Pin_1, R11.Pin_1, R12.Pin_1, R13.Pin_1, R14.Pin_1, R15.Pin_1, R16.Pin_1, R17.Pin_1, T-Extension1.3V3#0

notes:
  +

custom parts:
  T_Extension: T-Extension Board for RPi B+ and Rpi2 from SunFounder
