# Fritzing sketch Lesson 4  Breathing LED (saved by Fritzing 0.9.3b)
breadboards: 1

parts:
  R1 = Resistor [tolerance=±5% resistance=220 package=THT]
  LED1 = LED - 5mm [color="Red (633nm)" package="5 mm [THT]"]
  T-Extension1 = T_Extension

nets:
  N1: R1.Pin_0, LED1.anode
  N2: R1.Pin_1, T-Extension1.B18
  N3: LED1.cathode, T-Extension1.GND#36

notes:
  +

custom parts:
  T_Extension: T-Extension Board for RPi B+ and Rpi2 from SunFounder
