# Fritzing sketch Lesson 5  RGB LED (saved by Fritzing 0.9.1b)
breadboards: 1

parts:
  LED1 = RGB LED (com. cathode, rgb) [package="5 mm [THT]"]
  R4 = Resistor [tolerance=±5% resistance=220 package=THT]
  R3 = Resistor [tolerance=±5% resistance=220 package=THT]
  R2 = Resistor [tolerance=±5% resistance=220 package=THT]
  T-Extension1 = T_Extension

nets:
  N1: LED1.red_anode, R2.Pin_1
  N2: LED1.common_cathode, T-Extension1.GND#36
  N3: LED1.green_anode, R3.Pin_1
  N4: LED1.blue_anode, R4.Pin_1
  N5: R4.Pin_0, T-Extension1.B27
  N6: R3.Pin_0, T-Extension1.B18
  N7: R2.Pin_0, T-Extension1.B17

custom parts:
  T_Extension: T-Extension Board for RPi B+ and Rpi2 from SunFounder
