# Fritzing sketch Lesson 6  Buzzer (saved by Fritzing 0.8.7b)
breadboards: 1

parts:
  Q1 = PNP-Transistor [package="SOT-23 [SMD]"]
  J1 = Piezo Speaker
  R1 = Resistor [tolerance=±5% resistance=1k package=THT]
  T-Extension1 = T_Extension

nets:
  N1: Q1.2, J1.pin1
  N2: Q1.0, R1.Pin_1
  N3: Q1.1, T-Extension1.GND#36
  N4: J1.pin2, T-Extension1.5V
  N5: R1.Pin_0, T-Extension1.B17

custom parts:
  T_Extension: T-Extension Board for RPi B+ and Rpi2 from SunFounder
