# Fritzing sketch Lesson 7 Relay (saved by Fritzing 0.9.3b)
breadboards: 1

parts:
  Q1 = NPN-Transistor [package="TO92 [THT]"]
  D1 = Rectifier Diode [part_number=1N4001 package="300 mil [THT]"]
  LED1 = LED - 5mm [color="Red (633nm)" package="5 mm [THT]"]
  R3 = Resistor [tolerance=±5% resistance=1k package=THT]
  R2 = Resistor [tolerance=±5% resistance=220 package=THT]
  T-Extension1 = T_Extension
  K2 = Relay [part_number=FRS1B-S package=THT]

nets:
  N1: Q1.E, LED1.cathode, T-Extension1.GND#36
  N2: Q1.B, R3.Pin_0
  N3: Q1.C, D1.anode, K2.COIL1
  N4: D1.cathode, T-Extension1.5V, K2.C1, K2.C2, K2.COIL2
  N5: LED1.anode, R2.Pin_1
  N6: R3.Pin_1, T-Extension1.B17
  N7: R2.Pin_0, K2.B

custom parts:
  T_Extension: T-Extension Board for RPi B+ and Rpi2 from SunFounder
  Relay: An SPDT relay.
