# Fritzing sketch relay (saved by Fritzing 0.8.7b)
breadboards: 1

parts:
  K1 = Relay [part_number=FRS1B-S package=THT]
  Q1 = NPN-Transistor [package="TO92 [THT]"]
  D1 = Rectifier Diode [part_number=1N4001 package="300 mil [THT]"]
  LED1 = LED - 5mm [color="Red (633nm)" package="5 mm [THT]"]
  R3 = Resistor [tolerance=±5% resistance=1k package=THT]
  R2 = Resistor [tolerance=±5% resistance=220 package=THT]
  T-Extension1 = T_Extension

nets:
  N1: K1.COIL1, Q1.C, D1.anode
  N2: K1.C1, K1.C2, K1.COIL2, D1.cathode, T-Extension1.5V
  N3: K1.B, R2.Pin_0
  N4: Q1.E, LED1.cathode, T-Extension1.GND#36
  N5: Q1.B, R3.Pin_0
  N6: LED1.anode, R2.Pin_1
  N7: R3.Pin_1, T-Extension1.B17

custom parts:
  T_Extension: T-Extension Board for RPi B+ and Rpi2 from SunFounder
