# Fritzing sketch Lesson 8 4N35 (saved by Fritzing 0.9.3b)
breadboards: 1

parts:
  LED1 = LED - 5mm [color="Red (633nm)" package="5 mm [THT]"]
  R1 = Resistor [tolerance=±5% resistance=220 package=THT]
  R2 = Resistor [tolerance=±5% resistance=1k package=THT]
  U2 = 4N35 [package=THT]
  T-Extension2 = T_Extension

nets:
  N1: LED1.cathode, U2.Pin_5
  N2: LED1.anode, R1.Pin_0
  N3: R1.Pin_1, R2.Pin_1, T-Extension2.3V3#0
  N4: R2.Pin_0, U2.Pin_1
  N5: U2.Pin_2, T-Extension2.B17
  N6: U2.Pin_4, T-Extension2.GND#36

custom parts:
  4N35: Optocoupler - keeps you from frying your stuff!
  T_Extension: T-Extension Board for RPi B+ and Rpi2 from SunFounder
