# Fritzing sketch Lesson 8 4N35 (saved by Fritzing 0.8.7b)
breadboards: 1

parts:
  LED1 = LED - 5mm [color="Red (633nm)" package="5 mm [THT]"]
  R1 = Resistor [tolerance=±5% resistance=220 package=THT]
  R2 = Resistor [tolerance=±5% resistance=1k package=THT]
  T-Extension1 = T_Extension
  U2 = 4N35 [package=THT]

nets:
  N1: LED1.cathode, U2.Pin_5
  N2: LED1.anode, R1.Pin_0
  N3: R1.Pin_1, R2.Pin_1, T-Extension1.3V3#0
  N4: R2.Pin_0, U2.Pin_1
  N5: T-Extension1.B17, U2.Pin_2
  N6: T-Extension1.GND#36, U2.Pin_4

custom parts:
  T_Extension: T-Extension Board for RPi B+ and Rpi2 from SunFounder
  4N35: Optocoupler - keeps you from frying your stuff!
