# Fritzing sketch ne555 (saved by Fritzing 0.9.3b)
breadboards: 1

parts:
  NE555 = General purpose bipolar Timer [package=dil-08]
  C1 = Ceramic Capacitor [capacitance=100nF package="100 mil [THT, multilayer]"]
  R1 = Rotary Potentiometer (Small) [maximum_resistance=100kΩ package=THT]
  C2 = Ceramic Capacitor [capacitance=100nF package="100 mil [THT, multilayer]"]
  R2 = Resistor [tolerance=±5% resistance=10k package=THT]
  T-Extension1 = T_Extension

nets:
  N1: NE555.GND, C1.1, C2.1, T-Extension1.GND#36
  N2: NE555.TRI, NE555.TRE, C1.0, R1.leg1
  N3: NE555.OUT, T-Extension1.B18
  N4: NE555._RES, NE555.VCC+, R2.Pin_0, T-Extension1.5V
  N5: NE555.CON, C2.0
  N6: NE555.DIS, R1.wiper, R2.Pin_1

custom parts:
  T_Extension: T-Extension Board for RPi B+ and Rpi2 from SunFounder
